# Fritzing sketch Arduino breadboard (saved by Fritzing 0.9.6b)
circuit board: 8.46667cm x 5.64444cm
breadboards: 1

parts:
  R2 = Resistor [tolerance=±5% power=5 resistance=10k package=THT]
  R3 = Resistor [tolerance=±5% power=5W resistance=20k package=THT]
  Part1 = Arduino Mega 2560 (Rev3)
  LED1 = LED - 5mm [color="Red (633nm)" current=0.030 package="5 mm [THT]"]

nets:
  N1: R2.Pin_0, Part1.D13_PWM
  N2: R2.Pin_1, R3.Pin_0
  N3: R3.Pin_1, Part1.GND, LED1.anode
  N4: Part1.D12_PWM, LED1.cathode
